// Logisim project flip-flop-jk.circ as structural Verilog: 1 circuit, main circuit main
module main (
  input  in_1,
  input  in_2,
  input  in_3,
  input  in_4,
  output q1,
  output q0
);

  wire j_k_ff_1_qn, q0_tilde_qn;

  J_K_Flip_Flop j_k_ff_1 (
    .J(q0_tilde_qn), .clk(in_1), .K(q0), .Q(q1), .Qn(j_k_ff_1_qn), .preset(in_2), .en(in_3), .reset(in_4));
  J_K_Flip_Flop q0_tilde (.J(q1), .K(j_k_ff_1_qn), .Q(q0), .Qn(q0_tilde_qn));  // open: clk, preset, en, reset
endmodule
